// Logisim project alu_grey.circ as structural Verilog: 1 circuit, main circuit main
module main (
  input  [3:0] A,
  input  [3:0] B,
  input  [2:0] ALUSel,
  output [3:0] ALUResult,
  output OVFL,
  output OVFL_U
);

  wire ADD0, ADD1, ADD2, ADD3, adder_1_cout, adder_2_cout, adder_3_cout, adder_4_cout, AND0, AND1, AND2,
       AND3, NOT0, NOT1, NOT2, NOT3, OR0, OR1, OR2, OR3, XOR0, XOR1, XOR2, XOR3, xor_1_out, xor_2_out,
       xor_3_out, xor_4_out;

  xor xor_1 (xor_1_out, B[0], ALUSel[0]);
  xor xor_2 (xor_2_out, B[1], ALUSel[0]);
  xor xor_3 (xor_3_out, B[2], ALUSel[0]);
  xor xor_4 (xor_4_out, B[3], ALUSel[0]);
  Adder #(.width(1)) adder_1 (.a(A[0]), .b(xor_1_out), .out(ADD0), .cin(ALUSel[0]), .cout(adder_1_cout));
  Adder #(.width(1)) adder_2 (.a(A[1]), .b(xor_2_out), .out(ADD1), .cin(adder_1_cout), .cout(adder_2_cout));
  Adder #(.width(1)) adder_3 (.a(A[2]), .b(xor_3_out), .out(ADD2), .cin(adder_2_cout), .cout(adder_3_cout));
  Adder #(.width(1)) adder_4 (.a(A[3]), .b(xor_4_out), .out(ADD3), .cin(adder_3_cout), .cout(adder_4_cout));
  not not_1 (NOT0, A[0]);
  not not_2 (NOT1, A[1]);
  not not_3 (NOT2, A[2]);
  not not_4 (NOT3, A[3]);
  and and_1 (AND0, A[0], B[0]);
  and and_2 (AND1, A[1], B[1]);
  and and_3 (AND2, A[2], B[2]);
  and and_4 (AND3, A[3], B[3]);
  xor xor_5 (OVFL, adder_3_cout, adder_4_cout);
  xor xor_6 (OVFL_U, adder_4_cout, ALUSel[0]);
  or or_1 (OR0, A[0], B[0]);
  or or_2 (OR1, A[1], B[1]);
  or or_3 (OR2, A[2], B[2]);
  or or_4 (OR3, A[3], B[3]);
  xor xor_7 (XOR0, A[0], B[0]);
  xor xor_8 (XOR1, A[1], B[1]);
  xor xor_9 (XOR2, A[2], B[2]);
  xor xor_10 (XOR3, A[3], B[3]);
  Multiplexer #(.select(3)) multiplexer_1 (
    .in0(ADD0), .in1(ADD0), .in2(NOT0), .in3(AND0), .in4(OR0), .in5(XOR0), .in6(A[0]), .in7(B[0]),
    .out(ALUResult[0]), .sel(ALUSel));
  Multiplexer #(.select(3)) multiplexer_2 (
    .in0(ADD1), .in1(ADD1), .in2(NOT1), .in3(AND1), .in4(OR1), .in5(XOR1), .in6(A[1]), .in7(B[1]),
    .out(ALUResult[1]), .sel(ALUSel));
  Multiplexer #(.select(3)) multiplexer_3 (
    .in0(ADD2), .in1(ADD2), .in2(NOT2), .in3(AND2), .in4(OR2), .in5(XOR2), .in6(A[2]), .in7(B[2]),
    .out(ALUResult[2]), .sel(ALUSel));
  Multiplexer #(.select(3)) multiplexer_4 (
    .in0(ADD3), .in1(ADD3), .in2(NOT3), .in3(AND3), .in4(OR3), .in5(XOR3), .in6(A[3]), .in7(B[3]),
    .out(ALUResult[3]), .sel(ALUSel));

  // Other names for the same wires on the sheet: SUB0 = ADD0; SUB1 = ADD1; SUB2 = ADD2; SUB3 = ADD3
endmodule
